# Fritzing sketch dj_board (saved by Fritzing 0.9.4)
breadboards: 1

parts:
  TRS1 = Audio Jack (TRS) 3.5mm [package="4Ucon 08780 [THT]"]
  R1 = Trimmer Potentiometer [maximum_resistance=10kΩ package=THT]
  R2 = Trimmer Potentiometer [maximum_resistance=10kΩ package=THT]
  R3 = Trimmer Potentiometer [maximum_resistance=10kΩ package=THT]
  C1 = Tantalum Capacitor [capacitance="1 μF" package="D 7343 [SMD, tantalum]"]
  TRS2 = Audio Jack (TRS) 3.5mm [package="4Ucon 08780 [THT]"]
  R4 = Trimmer Potentiometer [maximum_resistance=10kΩ package=THT]
  R5 = Trimmer Potentiometer [maximum_resistance=10kΩ package=THT]
  C2 = Tantalum Capacitor [capacitance="1 μF" package="D 7343 [SMD, tantalum]"]

nets:
  N1: TRS1.Sleeve, R1.leg2, C1.-, TRS2.Sleeve, R4.leg2, C2.-
  N2: TRS1.Tip, R1.leg1
  N3: R1.wiper, R2.leg1
  N4: R2.wiper, R3.leg1, C1.+
  N5: R3.leg2, R5.wiper, C2.+
  N6: TRS2.Tip, R4.leg1
  N7: R4.wiper, R5.leg1

notes:
  To output jack
